# Fritzing sketch Hive Scale - ESP32 CH340 30Pins - 2023.12.05 (saved by Fritzing 0.9.10b)
breadboards: 2

parts:
  S1 = Load Sensor - 50kg [part_number=SEN-10245]
  S2 = Load Sensor - 50kg [part_number=SEN-10245]
  S3 = Load Sensor - 50kg [part_number=SEN-10245]
  S4 = Load Sensor - 50kg [part_number=SEN-10245]
  AM2 = AM2320 Humidity and Temperature Sensor [part_number="Adafruit #3721"]
  AM1 = AM2301 Humidity and Temperature Sensor
  ESP32_30Pin_Wroom_CH340_USB_TypeC1 = ESP32 30Pin Wroom CH340 USB TypeC
  JST_XH_4pin = JST XH 4A 2.54mm [package=THT]
  S5 = Momentary Switch [package=ksa_sealed_tac_switch]
  S6 = Momentary Switch [package=ksa_sealed_tac_switch]
  R1 = Resistor [tolerance=±5% resistance=10k package="0402 [SMD]"]
  R2 = Resistor [tolerance=±5% resistance=10k package="0402 [SMD]"]
  A1 = HX711 purple load cell amplifier

nets:
  N1: S1.B, S3.B
  N2: S1.W, S2.W
  N3: S1.R, JST_XH_4pin.pin2, A1.Pin_2
  N4: S2.B, S4.B
  N5: S2.R, JST_XH_4pin.pin4, A1.Pin_4
  N6: S3.W, S4.W
  N7: S3.R, JST_XH_4pin.pin3, A1.Pin_3
  N8: S4.R, JST_XH_4pin.pin1, A1.Pin_1
  VDD: AM2.VDD, AM1.VDD, ESP32_30Pin_Wroom_CH340_USB_TypeC1.3V3, S5.1, S6.1, A1.Pin_9
  N9: AM2.SDA, ESP32_30Pin_Wroom_CH340_USB_TypeC1.GPIO27
  GND: AM2.GND, AM1.GND, ESP32_30Pin_Wroom_CH340_USB_TypeC1.GND, A1.Pin_6
  N10: AM1.DATA, ESP32_30Pin_Wroom_CH340_USB_TypeC1.GPIO14
  N11: ESP32_30Pin_Wroom_CH340_USB_TypeC1.GPIO32, S5.3, R1.Pin_1
  N12: ESP32_30Pin_Wroom_CH340_USB_TypeC1.GPIO33, S6.3, R2.Pin_1
  N13: ESP32_30Pin_Wroom_CH340_USB_TypeC1.GPIO4, A1.Pin_7
  N14: ESP32_30Pin_Wroom_CH340_USB_TypeC1.GPIO17, A1.Pin_8
  N15: R1.Pin_0, R2.Pin_0

notes:
  Dénuder le câble RJ9 sur 24 cm.
  Laisser 35 cm de gaine.
  Du côté gainé, ajouter un connecteur JST XH 4 broches mâle. Les fils rouges des capteurs doivent être raccordés au RJ9 selon le code couleur :
  🔸 Rouge → E+
  🔸 Noir → E−
  🔸 Jaune → A−
  🔸 Vert → A+
  A-
  A+
  E-
  E+

custom parts:
  Load Sensor - 50kg: Half-wheatstone bridge Load Cell modified from the Fritzing Repo This load sensor, sometimes called a strain gauge, is the same one found in digital bathroom scales (you know, the ones you use in January for your New Year's resolutions, and then forget about a month later). This sensor can measure up to about 110 pounds.
  AM2320 Humidity and Temperature Sensor: AM2320 I2C Humidity and Temperature Sensor
  JST XH 4A 2.54mm: 4 Pin JST XH connector
  HX711 purple load cell amplifier: The SparkFun Load Cell Amplifier is a small breakout board for the HX711 IC that allows you to easily read load cells to measure weight.
